# Fritzing sketch Ladder Game am Raspberry Pi (saved by Fritzing 0.7.7b)
breadboards: 1

parts:
  Raspberry_Pi1 = Raspberry Pi (Model B)
  MCP1 = MCP23016 [package="DIP (Dual Inline) [THT]"]
  R1 = Resistor [tolerance=±5% resistance=3.9k package=THT]
  C1 = Ceramic Capacitor [capacitance=10pF package="100 mil [THT, multilayer]"]
  R3 = Resistor [tolerance=±5% resistance=220 package=THT]
  R4 = Resistor [tolerance=±5% resistance=220 package=THT]
  R5 = Resistor [tolerance=±5% resistance=220 package=THT]
  R6 = Resistor [tolerance=±5% resistance=220 package=THT]
  R7 = Resistor [tolerance=±5% resistance=220 package=THT]
  R8 = Resistor [tolerance=±5% resistance=220 package=THT]
  R9 = Resistor [tolerance=±5% resistance=220 package=THT]
  R10 = Resistor [tolerance=±5% resistance=220 package=THT]
  LED2 = LED - 5mm [color="Red (635nm)" package="5 mm [THT]"]
  S1 = Pushbutton [package="[THT]"]
  R11 = Resistor [tolerance=±5% resistance=10k package=THT]  # not connected
  LED3 = LED - 5mm [color="Green (565nm)" package="5 mm [THT]"]
  LED4 = LED - 5mm [color="Red (635nm)" package="5 mm [THT]"]
  LED5 = LED - 5mm [color="Green (565nm)" package="5 mm [THT]"]
  LED6 = LED - 5mm [color="Yellow (592nm)" package="5 mm [THT]"]
  LED7 = LED - 5mm [color="Yellow (592nm)" package="5 mm [THT]"]
  LED8 = LED - 5mm [color="Yellow (592nm)" package="5 mm [THT]"]
  LED9 = LED - 5mm [color="Yellow (592nm)" package="5 mm [THT]"]
  R12 = Resistor [tolerance=±5% resistance=1k package=THT]  # not connected

nets:
  5V: Raspberry_Pi1.5V, MCP1.VDD, R1.Pin_0, S1.Pin_3, S1.Pin_4
  N1: Raspberry_Pi1.SDA, MCP1.SDA
  N2: Raspberry_Pi1.SCL, MCP1.SCL
  N3: Raspberry_Pi1.GND, MCP1.A0, MCP1.A1, MCP1.A2, MCP1.VSS#18, R3.Pin_0, R4.Pin_0, R5.Pin_0, R6.Pin_0, R7.Pin_0, R8.Pin_0, R9.Pin_0, R10.Pin_0
  N4: MCP1.GP1.0, LED3.anode
  N5: MCP1.GP1.1, LED5.anode
  N6: MCP1.GP1.2, LED8.anode
  N7: MCP1.GP1.3, LED9.anode
  N8: MCP1.GP1.4, LED7.anode
  N9: MCP1.VSS#7, C1.1
  N10: MCP1.CLK, R1.Pin_1, C1.0
  N11: MCP1.GP1.5, LED6.anode
  N12: MCP1.GP1.6, LED4.anode
  N13: MCP1.GP1.7, LED2.anode
  N14: MCP1.GP0.7, S1.Pin_1, S1.Pin_2
  N15: R3.Pin_1, LED2.cathode
  N16: R4.Pin_1, LED4.cathode
  N17: R5.Pin_1, LED8.cathode
  N18: R6.Pin_1, LED5.cathode
  N19: R7.Pin_1, LED6.cathode
  N20: R8.Pin_1, LED7.cathode
  N21: R9.Pin_1, LED9.cathode
  N22: R10.Pin_1, LED3.cathode

notes:
  Statt blauer Drähte
  können 1k Widerstände
  benutzt werden

custom parts:
  Raspberry Pi (Model B): Raspberry Pi Single-board Computer, Model B
  MCP23016: An I2C BUS 16 bit I/O expander.
