# Fritzing sketch Test-Aufbau LED und Taster (saved by Fritzing 0.7.7b)
breadboards: 1

parts:
  Raspberry_Pi1 = Raspberry Pi (Model B)
  MCP1 = MCP23016 [package="DIP (Dual Inline) [THT]"]
  R1 = Resistor [tolerance=±5% resistance=3.9k package=THT]
  C1 = Ceramic Capacitor [capacitance=10pF package="100 mil [THT, multilayer]"]
  R3 = Resistor [tolerance=±5% resistance=220 package=THT]
  LED2 = LED - 5mm [color="Red (635nm)" package="5 mm [THT]"]
  S1 = Pushbutton [package="[THT]"]
  R11 = Resistor [tolerance=±5% resistance=10k package=THT]  # not connected
  R12 = Resistor [tolerance=±5% resistance=1k package=THT]  # not connected

nets:
  5V: Raspberry_Pi1.5V, MCP1.VDD, R1.Pin_0, S1.Pin_3, S1.Pin_4
  N1: Raspberry_Pi1.SDA, MCP1.SDA
  N2: Raspberry_Pi1.SCL, MCP1.SCL
  N3: Raspberry_Pi1.GND, MCP1.A0, MCP1.A1, MCP1.A2, MCP1.VSS#18, R3.Pin_0
  N4: MCP1.VSS#7, C1.1
  N5: MCP1.CLK, R1.Pin_1, C1.0
  N6: MCP1.GP1.7, LED2.anode
  N7: MCP1.GP0.7, S1.Pin_1, S1.Pin_2
  N8: R3.Pin_1, LED2.cathode

notes:
  Statt blauer Drähte
  können 1k Widerstände
  benutzt werden

custom parts:
  Raspberry Pi (Model B): Raspberry Pi Single-board Computer, Model B
  MCP23016: An I2C BUS 16 bit I/O expander.
